// Digital circuit CPU.dig as structural Verilog
module CPU (
  input  [3:0] in_1,
  output [7:0] Out
);

  wire alu_1_p5, Clock;
  wire [7:0] Out_t;
  wire [11:0] eepromdualport_1_d;

  EEPROMDualPort #(.AddrBits(4), .Bits(12)) eepromdualport_1 (
    .A(in_1), .Din({12{1'b0}}), .str(1'b0), .C(Clock), .ld(1'b1), .D(eepromdualport_1_d));
  Register #(.Bits(8)) register_1 (.D(Out_t), .C(Clock), .en(1'b1), .Q(Out));
  Button #(.activeLow("true")) button_1 (.out(Clock));
  // ALU alu_1: pin names not known; wires that end beside it: eepromdualport_1_d[3:0], eepromdualport_1_d[11:4], Out, Out_t, alu_1_p5
  LED led_1 (.in(alu_1_p5));
  Seven_Seg_Hex seven_seg_hex_1 (.d(Out[7:4]), .dp(1'b0));
  Seven_Seg_Hex seven_seg_hex_2 (.d(Out[3:0]), .dp(1'b0));

  // Other names for the same wires on the sheet: Reg[7:0] = Out

  // Notes on the sheet:
  //   contents of eepromdualport_1 (hex, n*v repeats v):
  //   20,33,32,5,4
endmodule
